// Logisim project Aula03.circ as structural Verilog: 8 circuits, main circuit Add_4
module Add_4 (
  input  [3:0] A,
  input  [3:0] B,
  input  in_3,
  output out_4,
  output [3:0] out_5
);

  wire add_1_2_out_5, add_1_3_out_5, add_1_4_out_5;

  Add_1 add_1_1 (.in_1(B[3]), .in_2(A[3]), .Vem_1(add_1_2_out_5), .out_4(out_5[3]), .out_5(out_4));
  Add_1 add_1_2 (.in_1(B[2]), .in_2(A[2]), .Vem_1(add_1_3_out_5), .out_4(out_5[2]), .out_5(add_1_2_out_5));
  Add_1 add_1_3 (.in_1(B[1]), .in_2(A[1]), .Vem_1(add_1_4_out_5), .out_4(out_5[1]), .out_5(add_1_3_out_5));
  Add_1 add_1_4 (.in_1(B[0]), .in_2(A[0]), .Vem_1(in_3), .out_4(out_5[0]), .out_5(add_1_4_out_5));
endmodule

module Add_1 (
  input  in_1,
  input  in_2,
  input  Vem_1,
  output out_4,
  output out_5
);

  wire and_1_out, and_2_out, or_1_out, xor_1_out;

  xor xor_1 (xor_1_out, in_1, in_2);
  or or_1 (or_1_out, in_2, in_2);
  xor xor_2 (out_4, xor_1_out, Vem_1);
  and and_1 (and_1_out, or_1_out, in_1);
  and and_2 (and_2_out, in_2, Vem_1);
  or or_2 (out_5, and_1_out, and_2_out);
endmodule

module main (
);

  DEC3x8 dec3x8_1 ();  // open: in_1, S0, S1, S2, S3, S4, S5, S6, S7
  Add_4 add_4_1 ();  // open: in_3, out_4, A, B, out_5
endmodule

module Sub_1 (
  input  A,
  input  B,
  input  C_in,
  output Sub,
  output C_out
);

  wire and_1_out, and_2_out, not_1_out, or_1_out, xor_1_out;

  not not_1 (not_1_out, A);
  xor xor_1 (xor_1_out, A, B);
  or or_1 (or_1_out, B, C_in);
  xor xor_2 (Sub, xor_1_out, C_in);
  and and_1 (and_1_out, or_1_out, not_1_out);
  and and_2 (and_2_out, B, C_in);
  or or_2 (C_out, and_1_out, and_2_out);
endmodule

module Sub_4 (
  input  [3:0] A,
  input  [3:0] B,
  input  C_in,
  output C_out,
  output [3:0] out_5
);

  wire sub_1_2_c_out, sub_1_3_c_out, sub_1_4_c_out;

  Sub_1 sub_1_1 (.A(A[3]), .B(B[3]), .C_in(sub_1_2_c_out), .Sub(out_5[3]), .C_out(C_out));
  Sub_1 sub_1_2 (.A(A[2]), .B(B[2]), .C_in(sub_1_3_c_out), .Sub(out_5[2]), .C_out(sub_1_2_c_out));
  Sub_1 sub_1_3 (.A(A[1]), .B(B[1]), .C_in(sub_1_4_c_out), .Sub(out_5[1]), .C_out(sub_1_3_c_out));
  Sub_1 sub_1_4 (.A(A[0]), .B(B[0]), .C_in(C_in), .Sub(out_5[0]), .C_out(sub_1_4_c_out));
endmodule

module Buff (
  input  [3:0] B,
  input  in_2,
  output [3:0] S
);

  assign S[3] = in_2 ? B[3] : 1'bz;  // Controlled_Buffer controlled_buffer_1
  assign S[1] = in_2 ? B[1] : 1'bz;  // Controlled_Buffer controlled_buffer_2
  assign S[2] = in_2 ? B[2] : 1'bz;  // Controlled_Buffer controlled_buffer_3
  assign S[0] = in_2 ? B[0] : 1'bz;  // Controlled_Buffer controlled_buffer_4
endmodule

module Buff_inv (
  input  [3:0] B,
  input  in_2,
  output [3:0] S
);

  assign S[3] = in_2 ? ~B[3] : 1'bz;  // Controlled_Inverter controlled_inverter_1
  assign S[2] = in_2 ? ~B[2] : 1'bz;  // Controlled_Inverter controlled_inverter_2
  assign S[1] = in_2 ? ~B[1] : 1'bz;  // Controlled_Inverter controlled_inverter_3
  assign S[0] = in_2 ? ~B[0] : 1'bz;  // Controlled_Inverter controlled_inverter_4
endmodule

module DEC3x8 (
  input  [2:0] in_1,
  output S0,
  output S1,
  output S2,
  output S3,
  output S4,
  output S5,
  output S6,
  output S7
);

  wire not_1_out, not_2_out, not_3_out, not_4_out, not_5_out, not_6_out, not_7_out, not_8_out, not_9_out,
       not_10_out, not_11_out, not_12_out;

  not not_1 (not_1_out, in_1[2]);
  not not_2 (not_2_out, in_1[1]);
  and and_1 (S0, not_1_out, not_2_out, not_3_out);
  not not_3 (not_3_out, in_1[0]);
  not not_4 (not_4_out, in_1[2]);
  not not_5 (not_5_out, in_1[1]);
  and and_2 (S1, not_4_out, not_5_out, in_1[0]);
  not not_6 (not_6_out, in_1[2]);
  and and_3 (S2, not_6_out, in_1[1], not_7_out);
  not not_7 (not_7_out, in_1[0]);
  not not_8 (not_8_out, in_1[2]);
  and and_4 (S3, not_8_out, in_1[1], in_1[0]);
  not not_9 (not_9_out, in_1[1]);
  and and_5 (S4, in_1[2], not_9_out, not_10_out);
  not not_10 (not_10_out, in_1[0]);
  and and_6 (S5, in_1[2], not_11_out, in_1[0]);
  not not_11 (not_11_out, in_1[1]);
  and and_7 (S6, in_1[2], in_1[1], not_12_out);
  not not_12 (not_12_out, in_1[0]);
  and and_8 (S7, in_1[2], in_1[1], in_1[0]);
endmodule
